# Fritzing sketch Receiver (saved by Fritzing 0.9.3b)
breadboards: 1

parts:
  Componente1 = Arduino Uno (Rev3)
  Componente2 = NRF24L01+ Breakout Board
  M1 = Dagu DGServo 9g (Top view) [part_number=RS001B]
  S1 = H-Bridge with L298N
  M3 = DC Motor
  M4 = DC Motor
  M5 = DC Motor
  M6 = DC Motor
  HC-SR04_Sensor_1 = HC-SR04 Ultrasonic Distance Sensor
  U1 = SWITCH-SPST-2 [package=r_sw_th]
  VCC1 = Battery
  M7 = Dagu DGServo 9g (Top view) [part_number=RS001B]

nets:
  N1: Componente1.A0, HC-SR04_Sensor_1.ECHO
  N2: Componente1.A1, HC-SR04_Sensor_1.TRIG
  N3: Componente1.A2, S1.IN4
  N4: Componente1.A3, S1.IN3
  N5: Componente1.D8, S1.IN1
  N6: Componente1.D9_PWM, Componente2.CE
  N7: Componente1.D10_PWM/SS, Componente2.CS
  N8: Componente1.D11_PWM/MOSI, Componente2.MOSI
  N9: Componente1.D12/MISO, Componente2.MISO
  N10: Componente1.D13/SCK, Componente2.SCK
  N11: Componente1.D3_PWM, M1.pulse
  N12: Componente1.D4, M7.pulse
  N13: Componente1.D5_PWM, S1.ENB
  N14: Componente1.D6_PWM, S1.ENA
  N15: Componente1.D7, S1.IN2
  VCC: Componente1.5V, Componente2.VCC, HC-SR04_Sensor_1.VCC
  GND: Componente1.GND, Componente2.GND, M1.gnd, S1.GND, HC-SR04_Sensor_1.GND, VCC1.-, M7.gnd
  VCC_2: M1.vcc, S1.5V, M7.vcc
  N16: S1.12V, U1.O
  N17: S1.M1-01, M3.pin_2, M4.pin_2
  N18: S1.M1-02, M3.pin_1, M4.pin_1
  N19: S1.M2-01, M5.pin_1, M6.pin_1
  N20: S1.M2-02, M5.pin_2, M6.pin_2
  N21: U1.P, VCC1.+

notes:
  Battery pack 12V

custom parts:
  H-Bridge with L298N: h-bridge
